# Fritzing sketch Scale (saved by Fritzing 0.9.3b)

parts:
  ESP8266 = NodeMCU V1.0
  SSD1306 = Grove OLED 128x96
  HX711 = HX711 Weighing Sensor Module
  1 = Round Pushbutton
  4 = Round Pushbutton
  part = Resistor [tolerance=±5% resistance=10k package=THT]
  part_2 = Resistor [tolerance=±5% resistance=10k package=THT]
  part_3 = Resistor [tolerance=±5% resistance=10k package=THT]
  part_4 = Resistor [tolerance=±5% resistance=10k package=THT]
  2 = Round Pushbutton
  3 = Round Pushbutton

nets:
  N1: ESP8266.D1, SSD1306.SCL
  N2: ESP8266.D2, SSD1306.SDA
  N3: ESP8266.D3, HX711.CK/TX
  N4: ESP8266.3V3, 1.leg1, 4.leg1, 2.leg1, 3.leg1
  GND: ESP8266.GND, SSD1306.GND, HX711.GND, part.Pin_1, part_2.Pin_1, part_3.Pin_1, part_4.Pin_1
  N5: ESP8266.D5, 1.leg0, part_2.Pin_0
  N6: ESP8266.D6, part.Pin_0, 2.leg0
  N7: ESP8266.D7, part_4.Pin_0, 3.leg0
  N8: ESP8266.D8, 4.leg0, part_3.Pin_0
  N9: ESP8266.RX, HX711.DO/RX
  VCC: SSD1306.VCC, HX711.VCC

custom parts:
  NodeMCU V1.0: ESP8266 based NodeMCU
